# Fritzing sketch Untitled Sketch 2 (saved by Fritzing 0.9.3b)
breadboards: 1

parts:
  Part1 = Arduino Mega 2560 (Rev3)
  RE1 = Rotary Encoder [package=THT]
  Part2 = Arduino Ethernet Shield (Rev3)
  LCD1 = LCD screen
  Part3 = Real Time Clock Module - DS1307 RTC Breakout Board
  TempCWU = DS18B20 1-Wire Temperature Sensor [part_number=DS18B20]
  TempCO = DS18B20 1-Wire Temperature Sensor [part_number=DS18B20]
  TempPowrót = DS18B20 1-Wire Temperature Sensor [part_number=DS18B20]
  U1 = MAX6675 [package=so08]
  8_Channel_Relay1 = 8 Channel Power Relay
  termostat = Header 3 [package=screwterminal-3.5mm-3_lock.007s]
  TempPodajnik = DS18B20 1-Wire Temperature Sensor [part_number=DS18B20]
  Power_plug1 = Power plug  # not connected
  R1 = Resistor [tolerance=±5% resistance=220 package=THT]  # not connected

nets:
  N1: Part1.A9, 8_Channel_Relay1.IN7
  N2: Part1.A10, 8_Channel_Relay1.IN5
  N3: Part1.A11, 8_Channel_Relay1.IN4
  N4: Part1.A13, 8_Channel_Relay1.IN3
  N5: Part1.A14, 8_Channel_Relay1.IN2
  N6: Part1.A15, 8_Channel_Relay1.IN1
  N7: Part1.D21/SCL, LCD1.R/W, Part3.SCL
  N8: Part1.D20/SDA, LCD1.E, Part3.SDA
  N9: Part1.D18/TX1, RE1.EncoderPinB
  N10: Part1.D15/RX3, RE1.EncoderPinA
  N11: Part1.D26, termostat.1
  N12: Part1.D34, RE1.EncoderPinC
  N13: Part1.D39, U1.SCK
  N14: Part1.D40, U1.MISO
  N15: Part1.D41, U1.CS
  N16: Part1.D47, termostat.3
  N17: Part2.D2, 8_Channel_Relay1.GND
  GND: TempCWU.GND, TempCO.GND, TempPowrót.GND, TempPodajnik.GND

custom parts:
  8 Channel Power Relay: An 8 channel power relay. The module operates at 5V.
