# Fritzing sketch Untitled Sketch 4 (saved by Fritzing 0.9.3b)

parts:
  Part1 = Arduino Mega ADK (Rev3)
  Part2 = Arduino Ethernet Shield (Rev3)
  8_Channel_Relay1 = 8 Channel Power Relay

nets:
  N1: Part1.AREF, Part2.AREF
  N2: Part1.IOREF, Part2.IOREF
  N3: Part1.RESET, Part2.RESET
  N4: Part1.D22, 8_Channel_Relay1.IN1

custom parts:
  8 Channel Power Relay: An 8 channel power relay. The module operates at 5V.
